# Fritzing sketch pcb_shield (saved by Fritzing 0.8.7b)
circuit board: 15.0889cm x 5.35406cm
breadboards: 1

parts:
  Part1 = Arduino Mega 2560 (Rev3)
  power_12V_IN = screw terminal, 2 pins
  power_5V_OUT = screw terminal, 2 pins
  power_5V_OUT2 = screw terminal, 2 pins
  encod_1 = female pin header, 5 pins [form="♀ (female)"]
  encod_2 = female pin header, 5 pins [form="♀ (female)"]
  encod_3 = female pin header, 5 pins [form="♀ (female)"]
  encod_4 = female pin header, 5 pins [form="♀ (female)"]
  Gimbal = male pin header, 3 pins [form="♂ (male)"]
  Servo1 = male pin header, 3 pins [form="♂ (male)"]
  Servo2 = male pin header, 3 pins [form="♂ (male)"]
  Servo3 = male pin header, 3 pins [form="♂ (male)"]
  Servo_pince = male pin header, 3 pins [form="♂ (male)"]
  12->5 = LM2596 step down module
  12->6_8 = LM2596 step down module
  12v+ = male pin header, 4 pins [form="♂ (male)"]
  12v- = male pin header, 4 pins [form="♂ (male)"]
  Grove-Avant_droit = female pin header, 4 pins [form="♀ (female)"]
  Grove-derriere_gauche = female pin header, 4 pins [form="♀ (female)"]
  Grove-derriere_droit = female pin header, 4 pins [form="♀ (female)"]
  Grove-Avant_gauche = female pin header, 4 pins [form="♀ (female)"]

nets:
  N1: Part1.D19/RX1, encod_4.pin3
  N2: Part1.D18/TX1, encod_3.pin3
  N3: Part1.D12_PWM, Servo_pince.pin1
  N4: Part1.D11_PWM, Servo3.pin1
  N5: Part1.D10_PWM, Servo2.pin1
  N6: Part1.D9_PWM, Servo1.pin1
  N7: Part1.D8_PWM, Gimbal.pin1
  N8: Part1.GND, power_12V_IN.pin2, power_5V_OUT.pin2, power_5V_OUT2.pin2, Gimbal.pin3, Servo1.pin3, Servo2.pin3, Servo3.pin3, Servo_pince.pin3, 12->5.OUT+, 12->6_8.OUT+, 12v-.pin1, 12v-.pin2, 12v-.pin3, 12v-.pin4, Grove-Avant_droit.pin1, Grove-derriere_gauche.pin1, Grove-derriere_droit.pin1, Grove-Avant_gauche.pin1
  N9: Part1.D2_PWM, encod_1.pin3
  N10: Part1.D3_PWM, encod_2.pin3
  N11: Part1.D4_PWM, Grove-derriere_droit.pin3
  N12: Part1.D5_PWM, Grove-derriere_gauche.pin3
  N13: Part1.D6_PWM, Grove-Avant_droit.pin3
  N14: Part1.D7_PWM, Grove-Avant_gauche.pin3
  N15: Part1.D23, Grove-Avant_gauche.pin4
  N16: Part1.D25, Grove-Avant_droit.pin4
  N17: Part1.D27, Grove-derriere_gauche.pin4
  N18: Part1.D29, Grove-derriere_droit.pin4
  N19: Part1.D31, encod_1.pin5
  N20: Part1.D33, encod_2.pin5
  N21: Part1.D35, encod_3.pin5
  N22: Part1.D37, encod_4.pin5
  N23: power_12V_IN.pin1, 12->5.IN+, 12->6_8.IN+, 12v+.pin1, 12v+.pin2, 12v+.pin3, 12v+.pin4
  N24: power_5V_OUT.pin1, power_5V_OUT2.pin1, encod_1.pin1, encod_1.pin4, encod_2.pin1, encod_2.pin4, encod_3.pin1, encod_3.pin4, encod_4.pin1, encod_4.pin4, Gimbal.pin2, Servo1.pin2, Servo2.pin2, Servo3.pin2, Servo_pince.pin2, 12->5.IN-, 12->5.OUT-, 12->6_8.IN-, 12->6_8.OUT-

notes:
  12V IN
  5V OUT
  6.8V OUT
  Grove motor control
  M1- 7&23
  M2- 6&25
  M3- 5&27
  M4- 4&29
  Motor encoders
  ENC1- 19&37
  ENC2- 18&35
  ENC3- 3&33
  ENC4- 2&31
  12v +
  12v -
  Pince
  q1
  q2
  q3
  Gimbal
  G V S
  -   +
  Dir Pwm - Gnd

custom parts:
  LM2596 step down module: LM2596 DC-DC step down power supply module 3 A.
